# Fritzing sketch prototyping (saved by Fritzing 0.9.3b)
breadboards: 1

parts:
  Composant2 = Arduino Nano (Rev3.0)
  Composant3 = Arduino Uno (Rev3)
  LED1 = LED - 5mm [color="Red (633nm)" package="5 mm [THT]"]
  LED2 = LED - 5mm [color="Green (570nm)" package="5 mm [THT]"]
  S1 = Pushbutton [package=THT]
  R1 = Rotary Potentiometer (Small) [maximum_resistance=100kΩ package=THT]

nets:
  VIN: Composant2.D2, Composant2.VIN, Composant3.VIN, S1.leg0, R1.wiper
  N1: Composant2.D8, S1.leg1
  N2: Composant2.D9, LED2.anode
  N3: Composant2.D10, LED1.anode
  GND: Composant2.GND, Composant3.GND, LED1.cathode, LED2.cathode
  N4: Composant2.A6, Composant2.A5, Composant3.A5/SCL
  N5: Composant2.A4, Composant3.A4/SDA
  N6: Composant2.A0, R1.leg2

// code stored in the sketch: master.ino
# master
#include <wWire.h>

# web server
